# Fritzing sketch RC_PID_Controller (saved by Fritzing 0.9.3b)

parts:
  Part1 = Arduino Uno (Rev3)
  J1 = Camdenboss CTB0158-2 [part_number=CTB0158-2 package=THT]
  J2 = Camdenboss CTB0158-2 [part_number=CTB0158-2 package=THT]
  J3 = Camdenboss CTB0158-2 [part_number=CTB0158-2 package=THT]
  BAT1 = BC9VPC [package=bc9vpc]
  M1 = DC Motor
  M2 = DC Motor
  J4 = Infrared Proximity Sensor
  J5 = Infrared Proximity Sensor
  J6 = Infrared Proximity Sensor
  U1 = POT [package=3362u]
  VCC1 = 4 x AAA Battery Mount

nets:
  N1: Part1.A0, J4.Vout
  N2: Part1.A1, J6.Vout
  N3: Part1.A2, J5.Vout
  N4: Part1.A5/SCL, U1.S
  GND: Part1.GND, J4.GND, J5.GND, J6.GND, U1.A, VCC1.-
  VCC: Part1.5V, J4.Vcc, J5.Vcc, J6.Vcc, U1.E
  N5: Part1.VIN, VCC1.+
  N6: J1.terminal_1, M1.pin_2
  N7: J1.terminal_2, M1.pin_1
  N8: J2.terminal_1, M2.pin_2
  N9: J2.terminal_2, M2.pin_1
  N10: J3.terminal_1, BAT1.V+
  N11: J3.terminal_2, BAT1.V-

notes:
  Arduino with Adafruit Motor Shield v 2.0
  M1
  M4
  Motor Vin
  Drive Motor
  Steering Motor
  Front Sensor
  Left Sensor
  Right Sensor
  Steering Potentiometer
